# Fritzing sketch Układ2 (saved by Fritzing 0.9.3b)
breadboards: 1

parts:
  Raspberry_Pi_1 = Raspberry Pi 3 [part_number=RPI-3-V1.2]
  Part1 = BH1750
  DHT11_1 = DHT11 module
  Part2 = FC-28 Soil Hygrometer Module - Probe
  Part3 = FC-28 Soil Hygrometer Module
  WATER_PUMP1 = water pump/motor  # not connected
  KY-1 = Keyes Relay [package=THT]
  D1 = Rectifier Diode [part_number=1N4001 package="300 mil [THT]"]
  D2 = Rectifier Diode [part_number=1N4001 package="300 mil [THT]"]

nets:
  VCC: Raspberry_Pi_1.3v3, Part1.VCC, DHT11_1.VCC, Part3.VCC
  N1: Raspberry_Pi_1.GPIO2, Part1.SDA
  N2: Raspberry_Pi_1.GPIO3, Part1.SCL
  N3: Raspberry_Pi_1.GPIO4, DHT11_1.DATA
  GND: Raspberry_Pi_1.GND, Part1.GND, DHT11_1.GND, Part3.GND, KY-1.ground
  N4: Raspberry_Pi_1.GPIO17, D1.anode
  N5: Raspberry_Pi_1.5V, KY-1.signal
  N6: Part2.POS, Part3.POS
  N7: Part2.NEG, Part3.NEG
  N8: Part3.DO, D2.anode
  N9: KY-1.power, D1.cathode, D2.cathode

custom parts:
  BH1750: Light Sensor
  DHT11 module: https://cdn-learn.adafruit.com/downloads/pdf/dht.pdf DHT11 black pcb module reference by:https://github.com/adafruit/Fritzing-Library/blob/master/parts/DHT11%20Humitidy%20and%20Temperature%20Sensor.fzpz
  FC-28 Soil Hygrometer Module - Probe: The FC-28 is a soil hygrometer module that uses the Texas Instruments LM393 comparator chip to provide an analog measurement of soil humidity.
  FC-28 Soil Hygrometer Module: The FC-28 is a soil hygrometer module that uses the Texas Instruments LM393 comparator chip to provide an analog measurement of soil humidity. The digital output is high when soil moisture is over a certain threshold, as determined by adjusting the potentiometer.
  water pump/motor: WATER PUMP BY ARDUBLOCKTR
  Keyes Relay: The Keyes 5V relay module is suitable for SCM development, home appliance control. It uses a 5V~12V TIL control signal which can control DC / AC signal.
